// Logisim project 1st & 2nd Canonical form.circ as structural Verilog: 1 circuit, main circuit main
module main (
  input  A,
  input  B,
  input  C,
  input  A_2,
  input  B_2,
  input  C_2,
  output F___A_prime_B_prime_C___BC_prime,
  output F___AB_prime_C___BC___B_prime_C_prime
);

  wire and_1_out, and_2_out, and_3_out, and_4_out, and_5_out, and_6_out, and_7_out, not_1_out, not_2_out,
       not_3_out, not_4_out, not_5_out, not_6_out, or_2_out;

  not not_1 (not_1_out, B_2);
  not not_2 (not_2_out, B_2);
  not not_3 (not_3_out, C_2);
  not not_4 (not_4_out, A);
  not not_5 (not_5_out, B);
  not not_6 (not_6_out, C);
  and and_1 (and_1_out, A_2, not_1_out);
  and and_2 (and_2_out, not_4_out, not_5_out);
  and and_3 (and_3_out, and_1_out, C_2);
  and and_4 (and_4_out, B_2, C_2);
  and and_5 (and_5_out, and_2_out, C);
  and and_6 (and_6_out, B, not_6_out);
  or or_1 (F___A_prime_B_prime_C___BC_prime, and_5_out, and_6_out);
  or or_2 (or_2_out, and_3_out, and_4_out);
  and and_7 (and_7_out, not_2_out, not_3_out);
  or or_3 (F___AB_prime_C___BC___B_prime_C_prime, or_2_out, and_7_out);

  // Notes on the sheet:
  //   B'
  //   B'
  //   C'
  //   A'
  //   B'
  //   C'
  //   AB'
  //   1st Canonical Form
  //   2nd Canonical Form
  //   BC
  //   A'B'C
  //   BC'
  //   AB'C
  //   AB'C + BC
  //   B'C'
endmodule
